# Fritzing sketch HC-SR04 (saved by Fritzing 0.8.7b)
breadboards: 1

parts:
  부품1 = Arduino Uno (Rev3)
  부품2 = SRF05 Ultrasonic Rangefinder

nets:
  N1: 부품1.D10_PWM/SS, 부품2.Echo
  N2: 부품1.D11_PWM/MOSI, 부품2.Trig
  5V: 부품1.5V, 부품2.VCC
  GND: 부품1.GND, 부품2.GND
